// Digital circuit main.dig as structural Verilog
module main (
);

  ALU alu_1 ();  // open: A, B, SU, EO, out, carry, zero, EQL
  REG_A reg_a_1 ();  // open: AI, AO, BUS_i, BUS_o
  REG_B reg_b_1 ();  // open: BUS_i, BUS_o, BI, BO
endmodule
